# Fritzing sketch Schematic Diagram (saved by Fritzing 0.9.3b)
breadboards: 1

parts:
  Part1 = Arduino Uno (Rev3)
  DHT1 = Humidity and Temperature Sensor DHT11
  Part2 = Soil Moisture Sensor
  YL-83_-_Detection_Board1 = YL-83 Rain Sensor - Detection Board
  YL-83_-_Control_Board1 = YL-83 Rain Sensor - Control Board
  Part3 = NRF24L01+ Breakout Board
  ESP32_-_Back1 = ESP32 - CAM
  IC1 = L293D [package=THT]
  M1 = DC Motor  # not connected
  M2 = DC Motor  # not connected
  VCC1 = 4 x AAA Battery Mount

nets:
  N1: Part1.A0, Part2.SIG
  N2: Part1.A1, YL-83_-_Control_Board1.AO
  N3: Part1.D8, Part3.CE
  N4: Part1.D9_PWM, IC1.In_1
  N5: Part1.D10_PWM/SS, IC1.Enable_1
  N6: Part1.D11_PWM/MOSI, Part3.MOSI
  N7: Part1.D12/MISO, Part3.MISO
  N8: Part1.D13/SCK, Part3.SCK
  GND: Part1.GND, DHT1.GND_1, Part2.GND, YL-83_-_Control_Board1.GND, Part3.GND, ESP32_-_Back1.GND, IC1.0V, VCC1.-
  N9: Part1.D2, IC1.In_4
  N10: Part1.D3_PWM, IC1.Enable_2
  N11: Part1.D4, DHT1.Data-signal
  N12: Part1.D5_PWM, IC1.In_3
  N13: Part1.D6_PWM, IC1.In_2
  N14: Part1.D7, Part3.CS
  3V3: Part1.3V3, Part3.VCC
  VCC: Part1.5V, DHT1.Vcc, Part2.VCC, YL-83_-_Control_Board1.VCC, ESP32_-_Back1.5V, IC1.+V
  N15: YL-83_-_Detection_Board1.POS, YL-83_-_Control_Board1.POS
  N16: YL-83_-_Detection_Board1.NEG, YL-83_-_Control_Board1.NEG

notes:
  Organic Agri-tech Terrace Farming
  Over On the Terrace
  Trio- ElectroFest
  HackFest 23

custom parts:
  Humidity and Temperature Sensor DHT11: Digital relative humidity & temperature sensor DHT11
  YL-83 Rain Sensor - Detection Board: The YL-83 is a rain sensor that has more resistance when dry and less resistance when wet. The module runs at 5V.
  YL-83 Rain Sensor - Control Board: The YL-83 is a rain sensor that has more resistance when dry and less resistance when wet. The module runs at 5V.
  ESP32 - CAM: The ESP32-CAM has a very competitive small-size camera module that can operate independently as a minimum system with a footprint of only 27*40.5*4.5mm and a deep sleep current of up to 6mA.

// code stored in the sketch: soil moisture.ino
void setup()
{
Serial.begin(9600);
pinMode(A0,INPUT);
}

void loop()
{
int val = analogRead(A0);
Serial.println(val);
delay(2000);
}
